# Fritzing sketch электроника (saved by Fritzing 0.9.3b)

parts:
  Часть1 = Arduino Nano (Rev3.0)
  Часть2 = HX711 Weighing Sensor Module
  Grove1 = Grove OLED 128x96
  RE1 = KY-040 Rotary encoder [package=THT]

nets:
  GND: Часть1.GND, Часть2.GND, Grove1.GND, RE1.GND
  N1: Часть1.D2, RE1.SW
  N2: Часть1.D3, RE1.DT
  N3: Часть1.D4, RE1.CLK
  N4: Часть1.D5, Часть2.CK/TX
  N5: Часть1.D6, Часть2.DO/RX
  VCC: Часть1.5V, Часть2.VCC, Grove1.VCC, RE1.Vcc
  N6: Часть1.A5, Grove1.SCL
  N7: Часть1.A4, Grove1.SDA

custom parts:
  KY-040 Rotary encoder: KY-040 Rotary Encoder with switch on breakout borad from AZ Delivery
